// Logisim project EdgeComputer.circ as structural Verilog
module Immediate (
  input  invert,
  input  decr,
  input  [3:0] \bit ,
  output [15:0] out_4
);

  wire not_1_out, not_2_out;
  wire [15:0] decoder_1_out0, subtractor_1_out;

  not not_1 (not_1_out, decr);
  Decoder #(.select(4), .disabled(0), .enable("false")) decoder_1 (
    .out0(decoder_1_out0[0]), .out1(decoder_1_out0[1]), .out2(decoder_1_out0[2]), .out3(decoder_1_out0[3]),
    .out4(decoder_1_out0[4]), .out5(decoder_1_out0[5]), .out6(decoder_1_out0[6]), .out7(decoder_1_out0[7]),
    .out8(decoder_1_out0[8]), .out9(decoder_1_out0[9]), .out10(decoder_1_out0[10]),
    .out11(decoder_1_out0[11]), .out12(decoder_1_out0[12]), .out13(decoder_1_out0[13]),
    .out14(decoder_1_out0[14]), .out15(decoder_1_out0[15]), .sel(\bit ));
  Subtractor #(.width(16)) subtractor_1 (
    .a(decoder_1_out0), .b({16{1'b0}}), .out(subtractor_1_out), .bin(not_1_out));  // open: bout
  not not_2 (not_2_out, invert);
  assign out_4 = not_2_out ? subtractor_1_out : 16'bz;  // Controlled_Buffer controlled_buffer_1
  assign out_4 = invert ? ~subtractor_1_out : 16'bz;  // Controlled_Inverter controlled_inverter_1
endmodule

module SN74172 (
  input  CLK,
  input  [15:0] D0,
  input  W0,
  input  R0,
  input  [2:0] WA0,
  input  [2:0] RA0,
  input  [15:0] D1,
  input  R1,
  input  W1,
  input  [2:0] A2,
  output [15:0] Q0,
  output [15:0] Q1
);

  wire decoder_1_out0, decoder_1_out1, decoder_1_out2, decoder_1_out3, decoder_1_out4, decoder_1_out5,
       decoder_1_out6, decoder_1_out7, decoder_2_out0, decoder_2_out1, decoder_2_out2, decoder_2_out3,
       decoder_2_out4, decoder_2_out5, decoder_2_out6, decoder_2_out7;
  wire [15:0] muxed_latch_1_q, muxed_latch_2_q, muxed_latch_3_q, muxed_latch_4_q, muxed_latch_5_q,
       muxed_latch_6_q, muxed_latch_7_q, muxed_latch_8_q;

  Decoder #(.select(3), .disabled(0)) decoder_1 (
    .out0(decoder_1_out0), .out1(decoder_1_out1), .out2(decoder_1_out2), .out3(decoder_1_out3),
    .out4(decoder_1_out4), .out5(decoder_1_out5), .out6(decoder_1_out6), .out7(decoder_1_out7), .sel(WA0),
    .en(W0));
  Decoder #(.select(3), .disabled(0)) decoder_2 (
    .out0(decoder_2_out0), .out1(decoder_2_out1), .out2(decoder_2_out2), .out3(decoder_2_out3),
    .out4(decoder_2_out4), .out5(decoder_2_out5), .out6(decoder_2_out6), .out7(decoder_2_out7), .sel(A2),
    .en(W1));
  Muxed_Latch muxed_latch_1 (
    .D0(D0), .D1(D1), .W0(decoder_1_out0), .W1(decoder_2_out0), .CLK(CLK), .Q(muxed_latch_1_q));
  Muxed_Latch muxed_latch_2 (
    .D0(D0), .D1(D1), .W0(decoder_1_out1), .W1(decoder_2_out1), .CLK(CLK), .Q(muxed_latch_2_q));
  Muxed_Latch muxed_latch_3 (
    .D0(D0), .D1(D1), .W0(decoder_1_out2), .W1(decoder_2_out2), .CLK(CLK), .Q(muxed_latch_3_q));
  Muxed_Latch muxed_latch_4 (
    .D0(D0), .D1(D1), .W0(decoder_1_out3), .W1(decoder_2_out3), .CLK(CLK), .Q(muxed_latch_4_q));
  Muxed_Latch muxed_latch_5 (
    .D0(D0), .D1(D1), .W0(decoder_1_out4), .W1(decoder_2_out4), .CLK(CLK), .Q(muxed_latch_5_q));
  Muxed_Latch muxed_latch_6 (
    .D0(D0), .D1(D1), .W0(decoder_1_out5), .W1(decoder_2_out5), .CLK(CLK), .Q(muxed_latch_6_q));
  Muxed_Latch muxed_latch_7 (
    .D0(D0), .D1(D1), .W0(decoder_1_out6), .W1(decoder_2_out6), .CLK(CLK), .Q(muxed_latch_7_q));
  Muxed_Latch muxed_latch_8 (
    .D0(D0), .D1(D1), .W0(decoder_1_out7), .W1(decoder_2_out7), .CLK(CLK), .Q(muxed_latch_8_q));
  Multiplexer #(.select(3), .width(16)) multiplexer_1 (
    .in0(muxed_latch_1_q), .in1(muxed_latch_2_q), .in2(muxed_latch_3_q), .in3(muxed_latch_4_q),
    .in4(muxed_latch_5_q), .in5(muxed_latch_6_q), .in6(muxed_latch_7_q), .in7(muxed_latch_8_q), .out(Q0),
    .sel(RA0), .en(R0));
  Multiplexer #(.select(3), .width(16)) multiplexer_2 (
    .in0(muxed_latch_1_q), .in1(muxed_latch_2_q), .in2(muxed_latch_3_q), .in3(muxed_latch_4_q),
    .in4(muxed_latch_5_q), .in5(muxed_latch_6_q), .in6(muxed_latch_7_q), .in7(muxed_latch_8_q), .out(Q1),
    .sel(A2), .en(R1));
endmodule

module Muxed_Latch (
  input  [15:0] D0,
  input  [15:0] D1,
  input  W0,
  input  W1,
  input  CLK,
  output [15:0] Q
);

  wire or_1_out;
  wire [15:0] multiplexer_1_out;

  Multiplexer #(.width(16), .disabled(0), .enable("false")) multiplexer_1 (
    .in0(D1), .in1(D0), .out(multiplexer_1_out), .sel(W0));
  or or_1 (or_1_out, W0, W1);
  Register #(.width(16)) register_1 (.D(multiplexer_1_out), .en(or_1_out), .Q(Q), .clk(CLK));  // open: clr
endmodule
